// Logisim project 1A.circ as structural Verilog: 1 circuit, main circuit main
module main (
  input  A,
  input  B,
  input  C,
  output F
);

  wire nor_1_out, nor_2_out, nor_3_out, nor_4_out, nor_5_out, nor_6_out, nor_7_out, nor_8_out, nor_9_out,
       nor_10_out, nor_11_out, nor_12_out, nor_13_out, nor_14_out, nor_15_out, nor_16_out, nor_17_out,
       nor_18_out, nor_19_out, nor_20_out, nor_21_out, nor_22_out;

  nor nor_1 (nor_1_out, C, C);
  nor nor_2 (nor_2_out, C, C);
  nor nor_3 (nor_3_out, B, B);
  nor nor_4 (nor_4_out, C, C);
  nor nor_5 (nor_5_out, A, A);
  nor nor_6 (nor_6_out, C, C);
  nor nor_7 (nor_7_out, B, B);
  nor nor_8 (nor_8_out, A, A);
  nor nor_9 (nor_9_out, B, B);
  nor nor_10 (nor_10_out, A, B, nor_1_out);
  nor nor_11 (nor_11_out, A, B, nor_2_out);
  nor nor_12 (nor_12_out, A, nor_3_out, nor_4_out);
  nor nor_13 (nor_13_out, nor_5_out, nor_3_out, C);
  nor nor_14 (nor_14_out, nor_5_out, nor_3_out, nor_6_out);
  nor nor_15 (nor_15_out, A, A);
  nor nor_16 (nor_16_out, nor_7_out, C);
  nor nor_17 (nor_17_out, nor_8_out, nor_9_out);
  nor nor_18 (nor_18_out, nor_10_out, nor_11_out, nor_12_out, nor_13_out);
  nor nor_19 (nor_19_out, nor_14_out, nor_15_out, nor_16_out, nor_17_out);
  nor nor_20 (nor_20_out, nor_18_out, nor_18_out);
  nor nor_21 (nor_21_out, nor_19_out, nor_19_out);
  nor nor_22 (nor_22_out, nor_20_out, nor_21_out);
  nor nor_23 (F, nor_22_out, nor_22_out);

  // Notes on the sheet:
  //   A'B'C
  //   A'BC
  //   ABC'
  //   ABC
  //   A'B'
  //   BC'
  //   AB
  //   A'B'C
endmodule
