// Logisim project 1B.circ as structural Verilog: 1 circuit, main circuit main
module main (
  input  A,
  input  B,
  input  C,
  input  D,
  output F2
);

  wire nor_1_out, nor_2_out, nor_3_out, nor_4_out, nor_5_out, nor_6_out, nor_7_out, nor_8_out, nor_9_out,
       nor_10_out, nor_11_out, nor_12_out, nor_13_out, nor_14_out, nor_15_out, nor_16_out;

  nor nor_1 (nor_1_out, D, D);
  nor nor_2 (nor_2_out, D, D);
  nor nor_3 (nor_3_out, B, B);
  nor nor_4 (nor_4_out, D, D);
  nor nor_5 (nor_5_out, B, B);
  nor nor_6 (nor_6_out, D, D);
  nor nor_7 (nor_7_out, C, C);
  nor nor_8 (nor_8_out, A, A);
  nor nor_9 (nor_9_out, A, A);
  nor nor_10 (nor_10_out, nor_8_out, B, C, nor_2_out);
  nor nor_11 (nor_11_out, A, nor_3_out, C, nor_4_out);
  nor nor_12 (nor_12_out, nor_9_out, nor_5_out, C, nor_6_out);
  nor nor_13 (nor_13_out, A, B, C, nor_1_out);
  nor nor_14 (nor_14_out, A, nor_5_out, nor_7_out, nor_6_out);
  nor nor_15 (nor_15_out, nor_9_out, nor_5_out, nor_7_out, nor_6_out);
  nor nor_16 (nor_16_out, nor_13_out, nor_10_out, nor_11_out, nor_12_out, nor_14_out, nor_15_out);
  nor nor_17 (F2, nor_16_out, nor_16_out);

  // Notes on the sheet:
  //   AB'C'D
  //   A'BC'D
  //   ABC'D
  //   A'BCD
  //   A'B'C'D
  //   ABCD
endmodule
