// Logisim project 2B.circ as structural Verilog: 1 circuit, main circuit main
module main (
  input  A,
  input  B,
  input  C,
  input  D,
  output F2
);

  wire nand_1_out, nand_2_out, nand_3_out, nand_4_out, nand_5_out, nand_6_out, nand_7_out, nand_8_out,
       nand_9_out, nand_10_out, nand_11_out, nand_12_out, nand_13_out, nand_14_out, nand_15_out;

  nand nand_1 (nand_1_out, A, A);
  nand nand_2 (nand_2_out, B, B);
  nand nand_3 (nand_3_out, C, C);
  nand nand_4 (nand_4_out, B, B);
  nand nand_5 (nand_5_out, C, C);
  nand nand_6 (nand_6_out, A, A);
  nand nand_7 (nand_7_out, C, C);
  nand nand_8 (nand_8_out, C, C);
  nand nand_9 (nand_9_out, A, A);
  nand nand_10 (nand_10_out, A, nand_4_out, nand_5_out, D);
  nand nand_11 (nand_11_out, nand_6_out, B, nand_7_out, D);
  nand nand_12 (nand_12_out, A, B, nand_8_out, D);
  nand nand_13 (nand_13_out, nand_1_out, nand_2_out, nand_3_out, D);
  nand nand_14 (nand_14_out, nand_9_out, B, C, D);
  nand nand_15 (nand_15_out, A, B, C, D);
  nand nand_16 (F2, nand_13_out, nand_10_out, nand_11_out, nand_12_out, nand_14_out, nand_15_out);

  // Notes on the sheet:
  //   A'
  //   B'
  //   C'
  //   B'
  //   C'
  //   A'
  //   C'
  //   C'
  //   A'
  //   AB'C'D
  //   A'BC'D
  //   ABC'D
  //   A'BCD
  //   A'B'C'D
  //   ABCD
endmodule
