// Logisim project 2D.circ as structural Verilog: 1 circuit, main circuit main
module main (
  input  x,
  input  y,
  input  z,
  output F4
);

  wire nand_1_out, nand_2_out, nand_3_out, nand_4_out, nand_5_out, nand_6_out, nand_7_out, nand_8_out,
       nand_9_out, nand_10_out, nand_11_out;

  nand nand_1 (nand_1_out, x, y, z);
  nand nand_2 (nand_2_out, x, y);
  nand nand_3 (nand_3_out, x, z);
  nand nand_4 (nand_4_out, y, z);
  nand nand_5 (nand_5_out, y, y);
  nand nand_6 (nand_6_out, nand_2_out, nand_3_out, nand_4_out);
  nand nand_7 (nand_7_out, x, x);
  nand nand_8 (nand_8_out, z, z);
  nand nand_9 (nand_9_out, nand_7_out, nand_5_out, nand_8_out);
  nand nand_10 (nand_10_out, nand_6_out, nand_6_out);
  nand nand_11 (nand_11_out, nand_10_out, nand_9_out);
  nand nand_12 (F4, nand_11_out, nand_1_out);

  // Notes on the sheet:
  //   xy
  //   xz
  //   yz
  //   xyz
  //   x+y+z
endmodule
