// Logisim project 3B.circ as structural Verilog: 1 circuit, main circuit main
module main (
  input  A,
  input  B,
  input  C,
  input  D,
  output F2
);

  wire and_1_out, and_2_out, and_3_out, and_4_out, and_5_out, and_6_out, not_1_out, not_2_out, not_3_out,
       not_4_out, not_5_out, not_6_out, not_7_out, not_8_out, not_9_out;

  not not_1 (not_1_out, A);
  not not_2 (not_2_out, B);
  not not_3 (not_3_out, C);
  not not_4 (not_4_out, B);
  not not_5 (not_5_out, C);
  not not_6 (not_6_out, A);
  not not_7 (not_7_out, C);
  not not_8 (not_8_out, C);
  not not_9 (not_9_out, A);
  and and_1 (and_1_out, not_6_out, B, not_7_out, D);
  and and_2 (and_2_out, A, B, not_8_out, D);
  and and_3 (and_3_out, not_1_out, not_2_out, not_3_out, D);
  and and_4 (and_4_out, A, not_4_out, not_5_out, D);
  and and_5 (and_5_out, not_9_out, B, C, D);
  and and_6 (and_6_out, A, B, C, D);
  or or_1 (F2, and_3_out, and_4_out, and_1_out, and_2_out, and_5_out, and_6_out);

  // Notes on the sheet:
  //   A'
  //   B'
  //   C'
  //   B'
  //   C'
  //   A'
  //   C'
  //   C'
  //   A'
  //   A'BC'D
  //   ABC'D
  //   A'BCD
  //   A'B'C'D
  //   AB'C'D
  //   ABCD
endmodule
