// Logisim project 3C.circ as structural Verilog: 1 circuit, main circuit main
module main (
  input  A,
  input  B,
  input  C,
  input  D,
  output out_5
);

  wire and_1_out, and_2_out, and_3_out, and_4_out, not_1_out, not_2_out, not_3_out, not_4_out, not_5_out;

  not not_1 (not_1_out, A);
  not not_2 (not_2_out, C);
  not not_3 (not_3_out, A);
  not not_4 (not_4_out, B);
  not not_5 (not_5_out, C);
  and and_1 (and_1_out, not_3_out, B, C, D);
  and and_2 (and_2_out, not_1_out, B, not_2_out, D);
  and and_3 (and_3_out, A, B);
  and and_4 (and_4_out, A, not_4_out, not_5_out, D);
  or or_1 (out_5, and_3_out, and_2_out, and_1_out, and_4_out);

  // Notes on the sheet:
  //   A'
  //   C'
  //   A'
  //   B'
  //   C'
  //   A'BCD
  //   A'BC'D
  //   AB
  //   AB'C'D
endmodule
