// Logisim project 3D.circ as structural Verilog: 1 circuit, main circuit main
module main (
  input  x,
  input  y,
  input  z,
  output F4
);

  wire and_1_out, and_2_out, and_3_out, and_4_out, and_5_out, not_1_out, or_1_out, or_2_out;

  and and_1 (and_1_out, x, y);
  and and_2 (and_2_out, x, z);
  and and_3 (and_3_out, y, z);
  or or_1 (or_1_out, and_1_out, and_2_out, and_3_out);
  not not_1 (not_1_out, or_1_out);
  or or_2 (or_2_out, x, y, z);
  and and_4 (and_4_out, x, y, z);
  and and_5 (and_5_out, not_1_out, or_2_out);
  or or_3 (F4, and_5_out, and_4_out);

  // Notes on the sheet:
  //   xy
  //   xz
  //   yz
  //   x+y+z
  //   xyz
endmodule
